// Digital circuit 2-bit-register-bank-example.dig as structural Verilog
module _2_bit_register_bank_example (
  input  clk,
  input  [7:0] D,
  input  en,
  input  [1:0] Address,
  output [7:0] Q
);

  wire and_1_out, and_2_out, and_3_out, and_4_out;
  wire [7:0] register_1_q, register_2_q, register_3_q, register_4_q;

  and and_1 (and_1_out, ~Address[0], ~Address[1], en);  // And
  and and_2 (and_2_out, Address[0], ~Address[1], en);  // And
  and and_3 (and_3_out, ~Address[0], Address[1], en);  // And
  and and_4 (and_4_out, Address[0], Address[1], en);
  Register #(.Bits(8)) register_1 (.D(D), .C(clk), .en(and_1_out), .Q(register_1_q));
  Register #(.Bits(8)) register_2 (.D(D), .C(clk), .en(and_2_out), .Q(register_2_q));
  Register #(.Bits(8)) register_3 (.D(D), .C(clk), .en(and_3_out), .Q(register_3_q));
  Register #(.Bits(8)) register_4 (.D(D), .C(clk), .en(and_4_out), .Q(register_4_q));
  Multiplexer #(.Bits(8), .Selector_Bits(2)) multiplexer_1 (
    .sel(Address), .in_0(register_1_q), .in_1(register_2_q), .in_2(register_3_q), .in_3(register_4_q), .out(Q));
endmodule
