// Digital circuit cpu.dig as structural Verilog
module cpu (
  input  clk,
  output [31:0] Current_instruction,
  output [31:0] PC,
  output [31:0] RS1,
  output [31:0] RS2,
  output [4:0] RSA,
  output [31:0] Alu_out,
  output [31:0] Mem_in,
  output [31:0] RDA,
  output Store_register,
  output Store_memory,
  output Load_alu,
  output Load_IMM,
  output Load_PC,
  output [4:0] RS1i,
  output [4:0] RS2i
);

  wire alu_1_zero, and_1_out, not_1_out, pc_signal_1_pc_alu, pc_signal_1_plus__imm;
  wire [2:0] signal_proc_1_func_3;
  wire [6:0] signal_proc_1_func_7;
  wire [31:0] add_1_s, add_2_s, data_d, imm_proc_1_imm, multiplexer_1_out, multiplexer_2_out,
       multiplexer_3_out, multiplexer_5_out;

  pc_signal pc_signal_1 (
    .Opcode(Current_instruction[6:0]), .Func_3(Current_instruction[14:12]), .Alu_out(Alu_out),
    .Zero_out(alu_1_zero), .PC_Alu(pc_signal_1_pc_alu), .plus__IMM(pc_signal_1_plus__imm));
  Add #(.Bits(32)) add_1 (.a(PC), .b(32'h4), .c_i(1'b0), .s(add_1_s));  // open: c_o
  Add #(.Bits(32)) add_2 (.a(PC), .b(imm_proc_1_imm), .c_i(1'b0), .s(add_2_s));  // open: c_o
  Multiplexer #(.Bits(32)) multiplexer_1 (
    .sel(pc_signal_1_plus__imm), .in_0(add_1_s), .in_1(add_2_s), .out(multiplexer_1_out));
  Multiplexer #(.Bits(32)) multiplexer_2 (
    .sel(pc_signal_1_pc_alu), .in_0(multiplexer_1_out), .in_1(Alu_out), .out(multiplexer_2_out));
  and and_1 (and_1_out, Current_instruction[0], Current_instruction[1]);
  Register #(.Bits(32), .isProgramCounter("true")) u_PC (.D(multiplexer_2_out), .C(clk), .en(and_1_out), .Q(PC));
  rom text (.A(PC), .sel(1'b1), .D(Current_instruction));
  imm_proc imm_proc_1 (.Instruction(Current_instruction), .IMM(imm_proc_1_imm));
  signal_proc signal_proc_1 (
    .Opcode(Current_instruction[6:0]), .Rem(Current_instruction[31:12]), .Func_7(signal_proc_1_func_7),
    .Func_3(signal_proc_1_func_3), .Reg_Store(Store_register), .Mem_Store(Store_memory), .Load_Lau(Load_alu),
    .Lau_IMM(Load_IMM), .Load_PC(Load_PC));
  register_bank register_bank_1 (
    .RS1i(Current_instruction[19:15]), .RS2i(Current_instruction[24:20]), .RSA(Current_instruction[11:7]),
    .CLK(clk), .RDA(RDA), .WR(Store_register), .RS1(RS1), .RS2(Mem_in));
  Multiplexer #(.Bits(32)) multiplexer_3 (
    .sel(Load_IMM), .in_0(Mem_in), .in_1(imm_proc_1_imm), .out(multiplexer_3_out));
  alu alu_1 (
    .A(RS1), .B(multiplexer_3_out), .OP3(signal_proc_1_func_3), .OP7(signal_proc_1_func_7), .R(Alu_out),
    .Zero(alu_1_zero));
  Multiplexer #(.Bits(32)) multiplexer_4 (.sel(Load_PC), .in_0(multiplexer_5_out), .in_1(add_1_s), .out(RDA));
  Multiplexer #(.Bits(32)) multiplexer_5 (.sel(Load_alu), .in_0(data_d), .in_1(Alu_out), .out(multiplexer_5_out));
  ram data (.A(Alu_out), .Din(Mem_in), .str(Store_memory), .clk(clk), .ld(not_1_out), .D(data_d));
  not not_1 (not_1_out, Store_memory);

  assign RS1i = Current_instruction[19:15];
  assign RS2 = Mem_in;
  assign RS2i = Current_instruction[24:20];
  assign RSA = Current_instruction[11:7];

  // Other names for the same wires on the sheet: ci[31:0] = Current_instruction; lau[31:0] = Alu_out; lc = Load_PC;
  //   li = Load_IMM; ll = Load_alu; mem[31:0] = Mem_in; ms = Store_memory; rs = Store_register

  // Notes on the sheet:
  //   Branch Func 3
  //   Debug values
  //   Halter
  //   Debug flags
  //   Imm
endmodule
