// Digital circuit imm-proc.dig as structural Verilog
module imm_proc (
  input  [31:0] Instruction,
  output [31:0] IMM
);

  wire and_1_out, and_2_out, and_3_out, and_4_out, nor_1_out, not_1_out, not_2_out, not_3_out, not_4_out,
       or_1_out, xor_1_out;
  wire [0:0] transgate_3_out1, transgate_4_out1;
  wire [10:0] transgate_4_out1_2;
  wire [19:0] transgate_1_out1, transgate_2_out1;
  wire [20:0] transgate_3_out1_2;

  xor xor_1 (xor_1_out, Instruction[2], Instruction[4]);
  nor nor_1 (nor_1_out, Instruction[5], Instruction[6]);
  and and_1 (and_1_out, ~Instruction[4], Instruction[5], ~Instruction[6]);  // And
  and and_2 (and_2_out, ~Instruction[2], ~Instruction[4], Instruction[5], Instruction[6]);  // And
  and and_3 (and_3_out, Instruction[2], Instruction[3], ~Instruction[4]);  // And
  and and_4 (and_4_out, ~Instruction[3], xor_1_out);  // And
  or or_1 (or_1_out, and_4_out, nor_1_out);
  not not_1 (not_1_out, or_1_out);
  TransGate #(.Bits(32)) transgate_1 (
    .A(or_1_out), .nA(not_1_out), .out1({transgate_1_out1, Instruction[31:20]}), .out2(IMM));
  not not_2 (not_2_out, and_1_out);
  TransGate #(.Bits(32)) transgate_2 (
    .A(and_1_out), .nA(not_2_out), .out1({transgate_2_out1, Instruction[31:25], Instruction[11:7]}),
    .out2(IMM));
  not not_3 (not_3_out, and_2_out);
  TransGate #(.Bits(32)) transgate_3 (
    .A(and_2_out), .nA(not_3_out),
    .out1({transgate_3_out1_2, Instruction[31], Instruction[7], Instruction[30:27], Instruction[11:8], transgate_3_out1[0]}),
    .out2(IMM));
  not not_4 (not_4_out, and_3_out);
  TransGate #(.Bits(32)) transgate_4 (
    .A(and_3_out), .nA(not_4_out),
    .out1({transgate_4_out1_2, Instruction[31], Instruction[21:12], Instruction[22], Instruction[30:23], transgate_4_out1[0]}),
    .out2(IMM));
  // also tied to GND on the sheet: {transgate_1_out1[0], transgate_1_out1[1], transgate_1_out1[2], transgate_1_out1[3], transgate_1_out1[4], transgate_1_out1[5], transgate_1_out1[6], transgate_1_out1[7], transgate_1_out1[8], transgate_1_out1[9], transgate_1_out1[10], transgate_1_out1[11], transgate_1_out1[12], transgate_1_out1[13], transgate_1_out1[14], transgate_1_out1[15], transgate_1_out1[16], transgate_1_out1[17], transgate_1_out1[18], transgate_1_out1[19], transgate_4_out1[0], transgate_2_out1[0], transgate_2_out1[1], transgate_2_out1[2], transgate_2_out1[3], transgate_2_out1[4], transgate_2_out1[5], transgate_2_out1[6], transgate_2_out1[7], transgate_2_out1[8], transgate_2_out1[9], transgate_2_out1[10], transgate_2_out1[11], transgate_2_out1[12], transgate_2_out1[13], transgate_2_out1[14], transgate_2_out1[15], transgate_2_out1[16], transgate_2_out1[17], transgate_2_out1[18], transgate_2_out1[19], transgate_3_out1[0], transgate_4_out1_2[0], transgate_4_out1_2[1], transgate_4_out1_2[2], transgate_4_out1_2[3], transgate_4_out1_2[4], transgate_4_out1_2[5], transgate_4_out1_2[6], transgate_4_out1_2[7], transgate_4_out1_2[8], transgate_4_out1_2[9], transgate_4_out1_2[10], transgate_3_out1_2[0], transgate_3_out1_2[1], transgate_3_out1_2[2], transgate_3_out1_2[3], transgate_3_out1_2[4], transgate_3_out1_2[5], transgate_3_out1_2[6], transgate_3_out1_2[7], transgate_3_out1_2[8], transgate_3_out1_2[9], transgate_3_out1_2[10], transgate_3_out1_2[11], transgate_3_out1_2[12], transgate_3_out1_2[13], transgate_3_out1_2[14], transgate_3_out1_2[15], transgate_3_out1_2[16], transgate_3_out1_2[17], transgate_3_out1_2[18], transgate_3_out1_2[19], transgate_3_out1_2[20]}

  // Notes on the sheet:
  //   I
  //   S
  //   B
  //   J
endmodule
