// Digital circuit lau.dig as structural Verilog
module lau (
  input  [31:0] A,
  input  [31:0] B,
  input  [2:0] OP3,
  input  [6:0] OP7,
  output [31:0] R,
  output Zero
);

  wire and_1_out, and_2_out, multiplexer_2_out, or_1_out;
  wire [31:0] add_1_s, and_3_out, barrelshifter_1_out, multiplexer_1_out, not_1_out, or_2_out, xor_1_out;

  and and_1 (and_1_out, OP7[5], ~OP3[0]);  // And
  and and_2 (and_2_out, OP3[1], ~OP3[2]);  // And
  or or_1 (or_1_out, and_1_out, and_2_out);
  assign not_1_out = ~B;  // Not not_1, 32 bits wide
  Multiplexer #(.Bits(32)) multiplexer_1 (.sel(or_1_out), .in_0(B), .in_1(not_1_out), .out(multiplexer_1_out));
  Multiplexer multiplexer_2 (.sel(or_1_out), .in_0(1'b0), .in_1(1'b1), .out(multiplexer_2_out));
  Add #(.Bits(32)) add_1 (.a(A), .b(multiplexer_1_out), .c_i(multiplexer_2_out), .s(add_1_s));  // open: c_o
  BarrelShifter #(.Bits(32), .barrelSigned("true")) barrelshifter_1 (.in(A), .shift(B[6:0]), .out(barrelshifter_1_out));
  assign xor_1_out = A ^ B;  // XOr xor_1, 32 bits wide
  assign or_2_out = A | B;  // Or or_2, 32 bits wide
  assign and_3_out = A & B;  // And and_3, 32 bits wide
  Multiplexer #(.Selector_Bits(3), .Bits(32)) multiplexer_3 (
    .sel(OP3), .in_0(add_1_s), .in_1(barrelshifter_1_out), .in_2(add_1_s), .in_3({32{1'b0}}),
    .in_4(xor_1_out), .in_5({32{1'b0}}), .in_6(or_2_out), .in_7(and_3_out), .out(R));
  nor nor_1 (Zero, R[0], R[1], R[2], R[3], R[4], R[5], R[6], R[7], R[8], R[9], R[10], R[11], R[12], R[13], R[14], R[15], R[16], R[17], R[18], R[19], R[20], R[21], R[22], R[23], R[24], R[25], R[26], R[27], R[28], R[29], R[30], R[31]);
endmodule
