// Digital circuit pc-signal.dig as structural Verilog
module pc_signal (
  input  [6:0] Opcode,
  input  [2:0] Func_3,
  input  [31:0] Alu_out,
  input  Zero_out,
  output PC_Alu,
  output plus__IMM
);

  wire and_1_out, and_2_out, and_3_out, multiplexer_1_out, not_1_out, not_2_out, or_1_out;

  not not_1 (not_1_out, Zero_out);
  not not_2 (not_2_out, Alu_out[31]);
  and and_1 (and_1_out, Opcode[5], Opcode[6]);
  and and_2 (and_2_out, Opcode[2], ~Opcode[3], ~Opcode[4]);  // And
  Multiplexer #(.Selector_Bits(3)) multiplexer_1 (
    .sel(Func_3), .in_0(Zero_out), .in_1(not_1_out), .in_2(1'b0), .in_3(not_2_out), .in_4(Alu_out[31]),
    .in_5(1'b0), .in_6(1'b0), .in_7(1'b0), .out(multiplexer_1_out));
  and and_3 (and_3_out, ~Opcode[2], Opcode[5], Opcode[6], multiplexer_1_out);  // And
  Multiplexer multiplexer_2 (.sel(and_1_out), .in_0(1'b0), .in_1(and_2_out), .out(PC_Alu));
  or or_1 (or_1_out, Opcode[3], and_3_out);
  Multiplexer multiplexer_3 (.sel(and_1_out), .in_0(1'b0), .in_1(or_1_out), .out(plus__IMM));
endmodule
