// Digital circuit ram.dig as structural Verilog
module ram (
  input  [31:0] A,
  input  [31:0] Din,
  input  str,
  input  clk,
  input  ld,
  output [31:0] D
);

  wire [7:0] multiplexer_1_out, multiplexer_2_out, multiplexer_3_out, multiplexer_4_out;
  wire [23:0] add_1_s, add_2_s, add_3_s, multiplexer_5_out, multiplexer_6_out, multiplexer_7_out;
  wire [31:0] ramdualport_1_d;

  Multiplexer #(.Bits(8), .Selector_Bits(2)) multiplexer_1 (
    .sel(A[1:0]), .in_0(Din[7:0]), .in_1(Din[15:8]), .in_2(Din[23:16]), .in_3(Din[31:24]),
    .out(multiplexer_1_out));
  Multiplexer #(.Selector_Bits(2), .Bits(8)) multiplexer_2 (
    .sel(A[1:0]), .in_0(Din[15:8]), .in_1(Din[23:16]), .in_2(Din[31:24]), .in_3(Din[7:0]),
    .out(multiplexer_2_out));
  Multiplexer #(.Selector_Bits(2), .Bits(8)) multiplexer_3 (
    .sel(A[1:0]), .in_0(Din[23:16]), .in_1(Din[31:24]), .in_2(Din[7:0]), .in_3(Din[15:8]),
    .out(multiplexer_3_out));
  Multiplexer #(.Selector_Bits(2), .Bits(8)) multiplexer_4 (
    .sel(A[1:0]), .in_0(Din[31:24]), .in_1(Din[7:0]), .in_2(Din[15:8]), .in_3(Din[23:16]),
    .out(multiplexer_4_out));
  Add #(.Bits(24)) add_1 (.a(A[25:2]), .b(24'h1), .c_i(1'b0), .s(add_1_s));  // open: c_o
  RAMDualPort #(.AddrBits(24), .Bits(8)) ramdualport_1 (
    .A(multiplexer_5_out), .Din(multiplexer_1_out), .str(str), .C(clk), .ld(ld), .D(ramdualport_1_d[15:8]));
  Add #(.Bits(24)) add_2 (.a(A[25:2]), .b(24'h1), .c_i(1'b0), .s(add_2_s));  // open: c_o
  RAMDualPort #(.AddrBits(24), .Bits(8)) ramdualport_2 (
    .A(multiplexer_6_out), .Din(multiplexer_2_out), .str(str), .C(clk), .ld(ld), .D(ramdualport_1_d[23:16]));
  Add #(.Bits(24)) add_3 (.a(A[25:2]), .b(24'h1), .c_i(1'b0), .s(add_3_s));  // open: c_o
  RAMDualPort #(.AddrBits(24), .Bits(8)) ramdualport_3 (
    .A(multiplexer_7_out), .Din(multiplexer_3_out), .str(str), .C(clk), .ld(ld), .D(ramdualport_1_d[31:24]));
  RAMDualPort #(.AddrBits(24), .Bits(8)) ramdualport_4 (
    .A(A[25:2]), .Din(multiplexer_4_out), .str(str), .C(clk), .ld(ld), .D(ramdualport_1_d[7:0]));
  Multiplexer #(.Bits(24), .Selector_Bits(2)) multiplexer_5 (
    .sel(A[1:0]), .in_0(A[25:2]), .in_1(add_1_s), .in_2(add_1_s), .in_3(add_1_s), .out(multiplexer_5_out));
  Multiplexer #(.Selector_Bits(2), .Bits(24)) multiplexer_6 (
    .sel(A[1:0]), .in_0(A[25:2]), .in_1(A[25:2]), .in_2(add_2_s), .in_3(add_2_s), .out(multiplexer_6_out));
  Multiplexer #(.Selector_Bits(2), .Bits(24)) multiplexer_7 (
    .sel(A[1:0]), .in_0(A[25:2]), .in_1(A[25:2]), .in_2(A[25:2]), .in_3(add_3_s), .out(multiplexer_7_out));
  Multiplexer #(.Bits(32), .Selector_Bits(2)) multiplexer_8 (
    .sel(A[1:0]), .in_0({ramdualport_1_d[7:0], ramdualport_1_d[31:8]}),
    .in_1({ramdualport_1_d[15:0], ramdualport_1_d[31:16]}),
    .in_2({ramdualport_1_d[23:0], ramdualport_1_d[31:24]}), .in_3(ramdualport_1_d), .out(D));
endmodule
