// Digital circuit register-bank.dig as structural Verilog
module register_bank (
  input  [4:0] RS1_2,
  input  [4:0] RS2,
  input  [4:0] RSA,
  input  CLK,
  input  [31:0] RDA,
  input  WR,
  output [31:0] RS1,
  output [31:0] RS2_2
);

  wire and_1_out, demultiplexer_2_out_1, demultiplexer_2_out_2, demultiplexer_2_out_3, demultiplexer_2_out_4,
       demultiplexer_2_out_5, demultiplexer_2_out_6, demultiplexer_2_out_7, demultiplexer_2_out_9,
       demultiplexer_2_out_10, demultiplexer_2_out_11, demultiplexer_2_out_12, demultiplexer_2_out_13,
       demultiplexer_2_out_14, demultiplexer_2_out_15, demultiplexer_2_out_16, demultiplexer_2_out_17,
       demultiplexer_2_out_18, demultiplexer_2_out_19, demultiplexer_2_out_20, demultiplexer_2_out_21,
       demultiplexer_2_out_22, demultiplexer_2_out_23, demultiplexer_2_out_24, demultiplexer_2_out_25,
       demultiplexer_2_out_26, demultiplexer_2_out_27, demultiplexer_2_out_28, demultiplexer_2_out_29,
       demultiplexer_2_out_30, demultiplexer_2_out_31;
  wire [31:0] demultiplexer_1_out_1, demultiplexer_1_out_2, demultiplexer_1_out_3, demultiplexer_1_out_4,
       demultiplexer_1_out_5, demultiplexer_1_out_6, demultiplexer_1_out_7, demultiplexer_1_out_8,
       demultiplexer_1_out_9, demultiplexer_1_out_10, demultiplexer_1_out_11, demultiplexer_1_out_12,
       demultiplexer_1_out_13, demultiplexer_1_out_14, demultiplexer_1_out_15, demultiplexer_1_out_16,
       demultiplexer_1_out_17, demultiplexer_1_out_18, demultiplexer_1_out_19, demultiplexer_1_out_20,
       demultiplexer_1_out_21, demultiplexer_1_out_22, demultiplexer_1_out_23, demultiplexer_1_out_24,
       demultiplexer_1_out_25, demultiplexer_1_out_26, demultiplexer_1_out_27, demultiplexer_1_out_28,
       demultiplexer_1_out_29, demultiplexer_1_out_30, demultiplexer_1_out_31, register_1_q, register_2_q,
       register_3_q, register_4_q, register_5_q, register_6_q, register_7_q, register_8_q, register_9_q,
       register_10_q, register_11_q, register_12_q, register_13_q, register_14_q, register_15_q,
       register_16_q, register_17_q, register_18_q, register_19_q, register_20_q, register_21_q,
       register_22_q, register_23_q, register_24_q, register_25_q, register_26_q, register_27_q,
       register_28_q, register_29_q, register_30_q, register_31_q;

  Demultiplexer #(.Selector_Bits(5), .Bits(32)) demultiplexer_1 (
    .sel(RSA), .in(RDA), .out_1(demultiplexer_1_out_1), .out_2(demultiplexer_1_out_2),
    .out_3(demultiplexer_1_out_3), .out_4(demultiplexer_1_out_4), .out_5(demultiplexer_1_out_5),
    .out_6(demultiplexer_1_out_6), .out_7(demultiplexer_1_out_7), .out_8(demultiplexer_1_out_8),
    .out_9(demultiplexer_1_out_9), .out_10(demultiplexer_1_out_10), .out_11(demultiplexer_1_out_11),
    .out_12(demultiplexer_1_out_12), .out_13(demultiplexer_1_out_13), .out_14(demultiplexer_1_out_14),
    .out_15(demultiplexer_1_out_15), .out_16(demultiplexer_1_out_16), .out_17(demultiplexer_1_out_17),
    .out_18(demultiplexer_1_out_18), .out_19(demultiplexer_1_out_19), .out_20(demultiplexer_1_out_20),
    .out_21(demultiplexer_1_out_21), .out_22(demultiplexer_1_out_22), .out_23(demultiplexer_1_out_23),
    .out_24(demultiplexer_1_out_24), .out_25(demultiplexer_1_out_25), .out_26(demultiplexer_1_out_26),
    .out_27(demultiplexer_1_out_27), .out_28(demultiplexer_1_out_28), .out_29(demultiplexer_1_out_29),
    .out_30(demultiplexer_1_out_30), .out_31(demultiplexer_1_out_31));  // open: out_0
  and and_1 (and_1_out, CLK, WR);
  Demultiplexer #(.Selector_Bits(5)) demultiplexer_2 (
    .sel(RSA), .in(and_1_out), .out_1(demultiplexer_2_out_1), .out_2(demultiplexer_2_out_2),
    .out_3(demultiplexer_2_out_3), .out_4(demultiplexer_2_out_4), .out_5(demultiplexer_2_out_5),
    .out_6(demultiplexer_2_out_6), .out_7(demultiplexer_2_out_7), .out_8(demultiplexer_2_out_7),
    .out_9(demultiplexer_2_out_9), .out_10(demultiplexer_2_out_10), .out_11(demultiplexer_2_out_11),
    .out_12(demultiplexer_2_out_12), .out_13(demultiplexer_2_out_13), .out_14(demultiplexer_2_out_14),
    .out_15(demultiplexer_2_out_15), .out_16(demultiplexer_2_out_16), .out_17(demultiplexer_2_out_17),
    .out_18(demultiplexer_2_out_18), .out_19(demultiplexer_2_out_19), .out_20(demultiplexer_2_out_20),
    .out_21(demultiplexer_2_out_21), .out_22(demultiplexer_2_out_22), .out_23(demultiplexer_2_out_23),
    .out_24(demultiplexer_2_out_24), .out_25(demultiplexer_2_out_25), .out_26(demultiplexer_2_out_26),
    .out_27(demultiplexer_2_out_27), .out_28(demultiplexer_2_out_28), .out_29(demultiplexer_2_out_29),
    .out_30(demultiplexer_2_out_30), .out_31(demultiplexer_2_out_31));  // open: out_0
  Register #(.Bits(32)) register_1 (.D(demultiplexer_1_out_1), .C(demultiplexer_2_out_1), .en(WR), .Q(register_1_q));
  Register #(.Bits(32)) register_2 (.D(demultiplexer_1_out_2), .C(demultiplexer_2_out_2), .en(WR), .Q(register_2_q));
  Register #(.Bits(32)) register_3 (.D(demultiplexer_1_out_3), .C(demultiplexer_2_out_3), .en(WR), .Q(register_3_q));
  Register #(.Bits(32)) register_4 (.D(demultiplexer_1_out_4), .C(demultiplexer_2_out_4), .en(WR), .Q(register_4_q));
  Register #(.Bits(32)) register_5 (.D(demultiplexer_1_out_5), .C(demultiplexer_2_out_5), .en(WR), .Q(register_5_q));
  Register #(.Bits(32)) register_6 (.D(demultiplexer_1_out_6), .C(demultiplexer_2_out_6), .en(WR), .Q(register_6_q));
  Register #(.Bits(32)) register_7 (.D(demultiplexer_1_out_7), .C(demultiplexer_2_out_7), .en(WR), .Q(register_7_q));
  Register #(.Bits(32)) register_8 (.D(demultiplexer_1_out_8), .C(demultiplexer_2_out_7), .en(WR), .Q(register_8_q));
  Register #(.Bits(32)) register_9 (.D(demultiplexer_1_out_9), .C(demultiplexer_2_out_9), .en(WR), .Q(register_9_q));
  Register #(.Bits(32)) register_10 (
    .D(demultiplexer_1_out_10), .C(demultiplexer_2_out_10), .en(WR), .Q(register_10_q));
  Register #(.Bits(32)) register_11 (
    .D(demultiplexer_1_out_11), .C(demultiplexer_2_out_11), .en(WR), .Q(register_11_q));
  Register #(.Bits(32)) register_12 (
    .D(demultiplexer_1_out_12), .C(demultiplexer_2_out_12), .en(WR), .Q(register_12_q));
  Register #(.Bits(32)) register_13 (
    .D(demultiplexer_1_out_13), .C(demultiplexer_2_out_13), .en(WR), .Q(register_13_q));
  Register #(.Bits(32)) register_14 (
    .D(demultiplexer_1_out_14), .C(demultiplexer_2_out_14), .en(WR), .Q(register_14_q));
  Register #(.Bits(32)) register_15 (
    .D(demultiplexer_1_out_15), .C(demultiplexer_2_out_15), .en(WR), .Q(register_15_q));
  Register #(.Bits(32)) register_16 (
    .D(demultiplexer_1_out_16), .C(demultiplexer_2_out_16), .en(WR), .Q(register_16_q));
  Register #(.Bits(32)) register_17 (
    .D(demultiplexer_1_out_17), .C(demultiplexer_2_out_17), .en(WR), .Q(register_17_q));
  Register #(.Bits(32)) register_18 (
    .D(demultiplexer_1_out_18), .C(demultiplexer_2_out_18), .en(WR), .Q(register_18_q));
  Register #(.Bits(32)) register_19 (
    .D(demultiplexer_1_out_19), .C(demultiplexer_2_out_19), .en(WR), .Q(register_19_q));
  Register #(.Bits(32)) register_20 (
    .D(demultiplexer_1_out_20), .C(demultiplexer_2_out_20), .en(WR), .Q(register_20_q));
  Register #(.Bits(32)) register_21 (
    .D(demultiplexer_1_out_21), .C(demultiplexer_2_out_21), .en(WR), .Q(register_21_q));
  Register #(.Bits(32)) register_22 (
    .D(demultiplexer_1_out_22), .C(demultiplexer_2_out_22), .en(WR), .Q(register_22_q));
  Register #(.Bits(32)) register_23 (
    .D(demultiplexer_1_out_23), .C(demultiplexer_2_out_23), .en(WR), .Q(register_23_q));
  Register #(.Bits(32)) register_24 (
    .D(demultiplexer_1_out_24), .C(demultiplexer_2_out_24), .en(WR), .Q(register_24_q));
  Register #(.Bits(32)) register_25 (
    .D(demultiplexer_1_out_25), .C(demultiplexer_2_out_25), .en(WR), .Q(register_25_q));
  Register #(.Bits(32)) register_26 (
    .D(demultiplexer_1_out_26), .C(demultiplexer_2_out_26), .en(WR), .Q(register_26_q));
  Register #(.Bits(32)) register_27 (
    .D(demultiplexer_1_out_27), .C(demultiplexer_2_out_27), .en(WR), .Q(register_27_q));
  Register #(.Bits(32)) register_28 (
    .D(demultiplexer_1_out_28), .C(demultiplexer_2_out_28), .en(WR), .Q(register_28_q));
  Register #(.Bits(32)) register_29 (
    .D(demultiplexer_1_out_29), .C(demultiplexer_2_out_29), .en(WR), .Q(register_29_q));
  Register #(.Bits(32)) register_30 (
    .D(demultiplexer_1_out_30), .C(demultiplexer_2_out_30), .en(WR), .Q(register_30_q));
  Register #(.Bits(32)) register_31 (
    .D(demultiplexer_1_out_31), .C(demultiplexer_2_out_31), .en(WR), .Q(register_31_q));
  Multiplexer #(.Bits(32), .Selector_Bits(5)) multiplexer_1 (
    .sel(RS2), .in_0({32{1'b0}}), .in_1(register_1_q), .in_2(register_2_q), .in_3(register_3_q),
    .in_4(register_4_q), .in_5(register_5_q), .in_6(register_6_q), .in_7(register_7_q), .in_8(register_8_q),
    .in_9(register_9_q), .in_10(register_10_q), .in_11(register_11_q), .in_12(register_12_q),
    .in_13(register_13_q), .in_14(register_14_q), .in_15(register_15_q), .in_16(register_16_q),
    .in_17(register_17_q), .in_18(register_18_q), .in_19(register_19_q), .in_20(register_20_q),
    .in_21(register_21_q), .in_22(register_22_q), .in_23(register_23_q), .in_24(register_24_q),
    .in_25(register_25_q), .in_26(register_26_q), .in_27(register_27_q), .in_28(register_28_q),
    .in_29(register_29_q), .in_30(register_30_q), .in_31(register_31_q), .out(RS2_2));
  Multiplexer #(.Selector_Bits(5), .Bits(32)) multiplexer_2 (
    .sel(RS1_2), .in_0({32{1'b0}}), .in_1(register_1_q), .in_2(register_2_q), .in_3(register_3_q),
    .in_4(register_4_q), .in_5(register_5_q), .in_6(register_6_q), .in_7(register_7_q), .in_8(register_8_q),
    .in_9(register_9_q), .in_10(register_10_q), .in_11(register_11_q), .in_12(register_12_q),
    .in_13(register_13_q), .in_14(register_14_q), .in_15(register_15_q), .in_16(register_16_q),
    .in_17(register_17_q), .in_18(register_18_q), .in_19(register_19_q), .in_20(register_20_q),
    .in_21(register_21_q), .in_22(register_22_q), .in_23(register_23_q), .in_24(register_24_q),
    .in_25(register_25_q), .in_26(register_26_q), .in_27(register_27_q), .in_28(register_28_q),
    .in_29(register_29_q), .in_30(register_30_q), .in_31(register_31_q), .out(RS1));
endmodule
