// Digital circuit rom.dig as structural Verilog
module rom (
  input  [31:0] A,
  input  sel,
  output [31:0] D
);

  wire [7:0] rom_3_d, rom_4_d;
  wire [15:0] rom_1_d;
  wire [23:0] add_1_s, add_2_s, add_3_s, multiplexer_1_out, multiplexer_2_out, multiplexer_3_out;

  Add #(.Bits(24)) add_1 (.a(A[25:2]), .b(24'h1), .c_i(1'b0), .s(add_1_s));  // open: c_o
  Add #(.Bits(24)) add_2 (.a(A[25:2]), .b(24'h1), .c_i(1'b0), .s(add_2_s));  // open: c_o
  Add #(.Bits(24)) add_3 (.a(A[25:2]), .b(24'h1), .c_i(1'b0), .s(add_3_s));  // open: c_o
  Multiplexer #(.Selector_Bits(2), .Bits(24)) multiplexer_1 (
    .sel(A[1:0]), .in_0(A[25:2]), .in_1(add_1_s), .in_2(add_1_s), .in_3(add_1_s), .out(multiplexer_1_out));
  Multiplexer #(.Selector_Bits(2), .Bits(24)) multiplexer_2 (
    .sel(A[1:0]), .in_0(A[25:2]), .in_1(A[25:2]), .in_2(add_2_s), .in_3(add_2_s), .out(multiplexer_2_out));
  Multiplexer #(.Selector_Bits(2), .Bits(24)) multiplexer_3 (
    .sel(A[1:0]), .in_0(A[25:2]), .in_1(A[25:2]), .in_2(A[25:2]), .in_3(add_3_s), .out(multiplexer_3_out));
  ROM #(.AddrBits(24), .Bits(8)) rom_1 (.A(multiplexer_1_out), .sel(sel), .D(rom_1_d[7:0]));
  ROM #(.AddrBits(24), .isProgramMemory("true"), .Bits(8)) rom_2 (.A(multiplexer_2_out), .sel(sel), .D(rom_1_d[15:8]));
  ROM #(.AddrBits(24), .isProgramMemory("true"), .Bits(8)) rom_3 (.A(multiplexer_3_out), .sel(sel), .D(rom_3_d));
  ROM #(.AddrBits(24), .isProgramMemory("true"), .Bits(8)) rom_4 (.A(A[25:2]), .sel(sel), .D(rom_4_d));
  Multiplexer #(.Selector_Bits(2), .Bits(32)) multiplexer_4 (
    .sel(A[1:0]), .in_0({rom_4_d, rom_3_d, rom_1_d}), .in_1({rom_1_d[7:0], rom_4_d, rom_3_d, rom_1_d[15:8]}),
    .in_2({rom_1_d, rom_4_d, rom_3_d}), .in_3({rom_3_d, rom_1_d, rom_4_d}), .out(D));

  // Notes on the sheet:
  //   rom_1 loads mod0.bin
  //   rom_2 loads mod1.bin
  //   rom_3 loads mod2.bin
  //   rom_4 loads mod3.bin
endmodule
