// Digital circuit load-store-model-example.dig as structural Verilog
module load_store_model_example (
  input  clk,
  input  [31:0] Instruction,
  output [7:0] Register,
  output [7:0] Mem
);

  wire not_1_out;
  wire [7:0] multiplexer_1_out;

  Multiplexer #(.Bits(8)) multiplexer_1 (
    .sel(Instruction[0]), .in_0(Mem), .in_1(Instruction[23:16]), .out(multiplexer_1_out));
  not not_1 (not_1_out, Instruction[1]);
  Register #(.Bits(8)) register_1 (.D(multiplexer_1_out), .C(clk), .en(Instruction[1]), .Q(Register));
  RAMDualPort #(.AddrBits(16), .Bits(8)) ramdualport_1 (
    .A(Instruction[31:16]), .Din(Register), .str(not_1_out), .C(clk), .ld(Instruction[1]), .D(Mem));
endmodule
